// Logisim project ETFStudent.circ as structural Verilog: 10 circuits, main circuit REG32_LD
module REG32_LD (
  input  [31:0] I15__0,
  input  LD,
  input  mr,
  input  CLK,
  output [31:0] A15__0
);

  // REG16_LD reg16_ld_1: pin names not known; wires that end beside it: CLK, mr, I15__0[31:16], A15__0[31:16], LD
  // REG16_LD reg16_ld_2: pin names not known; wires that end beside it: CLK, mr, I15__0[15:0], A15__0[15:0], LD

  // Notes on the sheet:
  //   __
endmodule

module KMADR (
  input  immed,
  input  memdir,
  input  regdir,
  input  regindpom,
  output [3:0] Adr3__0
);

  assign Adr3__0 = immed ? 4'b0010 : 4'bz;  // Controlled_Buffer controlled_buffer_1
  assign Adr3__0 = memdir ? 4'b0100 : 4'bz;  // Controlled_Buffer controlled_buffer_2
  assign Adr3__0 = regdir ? 4'b0101 : 4'bz;  // Controlled_Buffer controlled_buffer_3
  assign Adr3__0 = regindpom ? 4'b0111 : 4'bz;  // Controlled_Buffer controlled_buffer_4
endmodule

module KMOPR (
  input  LD,
  input  ST,
  input  ADD,
  input  SUB,
  input  BLSS,
  input  JLEQ,
  input  JMP,
  input  JSR,
  input  RTS,
  input  RTI,
  input  HALT,
  output [5:0] Adr5__0
);

  assign Adr5__0 = LD ? 6'b000010 : 6'bz;  // Controlled_Buffer controlled_buffer_1
  assign Adr5__0 = ST ? 6'b000100 : 6'bz;  // Controlled_Buffer controlled_buffer_2
  assign Adr5__0 = ADD ? 6'b001010 : 6'bz;  // Controlled_Buffer controlled_buffer_3
  assign Adr5__0 = SUB ? 6'b001100 : 6'bz;  // Controlled_Buffer controlled_buffer_4
  assign Adr5__0 = BLSS ? 6'b001110 : 6'bz;  // Controlled_Buffer controlled_buffer_5
  assign Adr5__0 = JLEQ ? 6'b010000 : 6'bz;  // Controlled_Buffer controlled_buffer_6
  assign Adr5__0 = JMP ? 6'b010001 : 6'bz;  // Controlled_Buffer controlled_buffer_7
  assign Adr5__0 = JSR ? 6'b010010 : 6'bz;  // Controlled_Buffer controlled_buffer_8
  assign Adr5__0 = RTS ? 6'b010111 : 6'bz;  // Controlled_Buffer controlled_buffer_9
  assign Adr5__0 = RTI ? 6'b011110 : 6'bz;  // Controlled_Buffer controlled_buffer_10
  assign Adr5__0 = HALT ? 6'b100010 : 6'bz;  // Controlled_Buffer controlled_buffer_11
endmodule

module REG6_INC_LD (
  input  [5:0] I5__0,
  input  LD,
  input  INC,
  input  mr,
  input  CLK,
  output [5:0] A5__0
);

  wire reg2m_inc_ld_1_p7, reg2m_inc_ld_2_p8;

  // REG2m_INC_LD reg2m_inc_ld_1: pin names not known; wires that end beside it: CLK, mr, I5__0[5:4], A5__0[5:4], LD, INC, reg2m_inc_ld_1_p7
  // REG2m_INC_LD reg2m_inc_ld_2: pin names not known; wires that end beside it: CLK, reg2m_inc_ld_1_p7, mr, I5__0[3:2], A5__0[3:2], LD, INC, reg2m_inc_ld_2_p8
  // REG2m_INC_LD reg2m_inc_ld_3: pin names not known; wires that end beside it: CLK, reg2m_inc_ld_2_p8, mr, I5__0[1:0], A5__0[1:0], LD, INC, INC

  // Notes on the sheet:
  //   __
endmodule

module GPR16X16 (
  input  [15:0] DI15__0,
  input  [3:0] A3__0,
  input  WR,
  input  CLK,
  output [15:0] DO15__0
);

  wire and_15_out, CS0, CS1, CS2, CS3, CS4, CS5, CS6, CS7, CS8, CS9, CS10, CS11, CS12, CS13, CS14, CS15,
       reg16_ld_1_p4, reg16_ld_2_p4, reg16_ld_3_p4, reg16_ld_4_p4, reg16_ld_5_p4, reg16_ld_6_p4,
       reg16_ld_7_p4, reg16_ld_8_p4, reg16_ld_9_p4, reg16_ld_10_p4, reg16_ld_11_p4, reg16_ld_12_p4,
       reg16_ld_13_p4, reg16_ld_14_p4, reg16_ld_16_p4;
  wire [15:0] reg16_ld_1_p3, reg16_ld_2_p3, reg16_ld_3_p3, reg16_ld_4_p3, reg16_ld_5_p3, reg16_ld_6_p3,
       reg16_ld_7_p3, reg16_ld_8_p3, reg16_ld_9_p3, reg16_ld_10_p3, reg16_ld_11_p3, reg16_ld_12_p3,
       reg16_ld_13_p3, reg16_ld_14_p3, reg16_ld_15_p3, reg16_ld_16_p3;

  // DC4_16 dc4_16_1: pin names not known; wires that end beside it: A3__0, 1'b1, CS0, CS1, CS2, CS3, CS4, CS5, CS6, CS7, CS8, CS9, CS10, CS11, CS12, CS13, CS14, CS15
  // REG16_LD reg16_ld_1: pin names not known; wires that end beside it: CLK, DI15__0, reg16_ld_1_p3, reg16_ld_1_p4
  assign DO15__0 = CS0 ? reg16_ld_1_p3 : 16'bz;  // Controlled_Buffer controlled_buffer_1
  // REG16_LD reg16_ld_2: pin names not known; wires that end beside it: CLK, DI15__0, reg16_ld_2_p3, reg16_ld_2_p4
  assign DO15__0 = CS1 ? reg16_ld_2_p3 : 16'bz;  // Controlled_Buffer controlled_buffer_2
  // REG16_LD reg16_ld_3: pin names not known; wires that end beside it: CLK, DI15__0, reg16_ld_3_p3, reg16_ld_3_p4
  assign DO15__0 = CS2 ? reg16_ld_3_p3 : 16'bz;  // Controlled_Buffer controlled_buffer_3
  // REG16_LD reg16_ld_4: pin names not known; wires that end beside it: CLK, DI15__0, reg16_ld_4_p3, reg16_ld_4_p4
  assign DO15__0 = CS3 ? reg16_ld_4_p3 : 16'bz;  // Controlled_Buffer controlled_buffer_4
  and and_1 (reg16_ld_1_p4, CS0, WR);
  and and_2 (reg16_ld_2_p4, CS1, WR);
  and and_3 (reg16_ld_3_p4, CS2, WR);
  and and_4 (reg16_ld_4_p4, CS3, WR);
  // REG16_LD reg16_ld_5: pin names not known; wires that end beside it: CLK, DI15__0, reg16_ld_5_p3, reg16_ld_5_p4
  and and_5 (reg16_ld_5_p4, CS4, WR);
  assign DO15__0 = CS4 ? reg16_ld_5_p3 : 16'bz;  // Controlled_Buffer controlled_buffer_5
  // REG16_LD reg16_ld_6: pin names not known; wires that end beside it: CLK, DI15__0, reg16_ld_6_p3, reg16_ld_6_p4
  and and_6 (reg16_ld_6_p4, CS5, WR);
  assign DO15__0 = CS5 ? reg16_ld_6_p3 : 16'bz;  // Controlled_Buffer controlled_buffer_6
  // REG16_LD reg16_ld_7: pin names not known; wires that end beside it: CLK, DI15__0, reg16_ld_7_p3, reg16_ld_7_p4
  and and_7 (reg16_ld_7_p4, CS6, WR);
  assign DO15__0 = CS6 ? reg16_ld_7_p3 : 16'bz;  // Controlled_Buffer controlled_buffer_7
  // REG16_LD reg16_ld_8: pin names not known; wires that end beside it: CLK, DI15__0, reg16_ld_8_p3, reg16_ld_8_p4
  and and_8 (reg16_ld_8_p4, CS7, WR);
  assign DO15__0 = CS7 ? reg16_ld_8_p3 : 16'bz;  // Controlled_Buffer controlled_buffer_8
  // REG16_LD reg16_ld_9: pin names not known; wires that end beside it: CLK, DI15__0, reg16_ld_9_p3, reg16_ld_9_p4
  assign DO15__0 = CS8 ? reg16_ld_9_p3 : 16'bz;  // Controlled_Buffer controlled_buffer_9
  // REG16_LD reg16_ld_10: pin names not known; wires that end beside it: CLK, DI15__0, reg16_ld_10_p3, reg16_ld_10_p4
  assign DO15__0 = CS9 ? reg16_ld_10_p3 : 16'bz;  // Controlled_Buffer controlled_buffer_10
  // REG16_LD reg16_ld_11: pin names not known; wires that end beside it: CLK, DI15__0, reg16_ld_11_p3, reg16_ld_11_p4
  assign DO15__0 = CS10 ? reg16_ld_11_p3 : 16'bz;  // Controlled_Buffer controlled_buffer_11
  // REG16_LD reg16_ld_12: pin names not known; wires that end beside it: CLK, DI15__0, reg16_ld_12_p3, reg16_ld_12_p4
  assign DO15__0 = CS11 ? reg16_ld_12_p3 : 16'bz;  // Controlled_Buffer controlled_buffer_12
  and and_9 (reg16_ld_9_p4, CS8, WR);
  and and_10 (reg16_ld_10_p4, CS9, WR);
  and and_11 (reg16_ld_11_p4, CS10, WR);
  and and_12 (reg16_ld_12_p4, CS11, WR);
  // REG16_LD reg16_ld_13: pin names not known; wires that end beside it: CLK, DI15__0, reg16_ld_13_p3, reg16_ld_13_p4
  and and_13 (reg16_ld_13_p4, CS12, WR);
  assign DO15__0 = CS12 ? reg16_ld_13_p3 : 16'bz;  // Controlled_Buffer controlled_buffer_13
  // REG16_LD reg16_ld_14: pin names not known; wires that end beside it: CLK, DI15__0, reg16_ld_14_p3, reg16_ld_14_p4
  and and_14 (reg16_ld_14_p4, CS13, WR);
  assign DO15__0 = CS13 ? reg16_ld_14_p3 : 16'bz;  // Controlled_Buffer controlled_buffer_14
  and and_15 (and_15_out, CS14, WR);
  // REG16_LD reg16_ld_15: pin names not known; wires that end beside it: CLK, DI15__0, reg16_ld_15_p3, and_15_out
  assign DO15__0 = CS14 ? reg16_ld_15_p3 : 16'bz;  // Controlled_Buffer controlled_buffer_15
  // REG16_LD reg16_ld_16: pin names not known; wires that end beside it: CLK, DI15__0, reg16_ld_16_p3, reg16_ld_16_p4
  and and_16 (reg16_ld_16_p4, CS15, WR);
  assign DO15__0 = CS15 ? reg16_ld_16_p3 : 16'bz;  // Controlled_Buffer controlled_buffer_16

  // Other names for the same wires on the sheet: inREG[15:0] = DI15__0; outREG[15:0] = DO15__0
endmodule

module KMOPREXEC (
  input  HALT,
  input  RTS,
  input  RTI,
  input  ROR,
  input  PUSH,
  input  POP,
  input  BOVF,
  input  BNCR,
  input  BLEQ,
  input  BLSSU,
  input  JLEQ,
  input  JMP,
  input  JSR,
  input  LD,
  input  ST,
  input  DEC,
  input  SUB,
  input  XOR,
  input  AND,
  input  STRFIND,
  output [7:0] Adr7__0
);

  assign Adr7__0 = HALT ? 8'h2 : 8'bz;  // Controlled_Buffer controlled_buffer_1
  assign Adr7__0 = RTS ? 8'h3 : 8'bz;  // Controlled_Buffer controlled_buffer_2
  assign Adr7__0 = RTI ? 8'h9 : 8'bz;  // Controlled_Buffer controlled_buffer_3
  assign Adr7__0 = ROR ? 8'hf : 8'bz;  // Controlled_Buffer controlled_buffer_4
  assign Adr7__0 = PUSH ? 8'h10 : 8'bz;  // Controlled_Buffer controlled_buffer_5
  assign Adr7__0 = POP ? 8'h16 : 8'bz;  // Controlled_Buffer controlled_buffer_6
  assign Adr7__0 = BOVF ? 8'h1d : 8'bz;  // Controlled_Buffer controlled_buffer_7
  assign Adr7__0 = BNCR ? 8'h1f : 8'bz;  // Controlled_Buffer controlled_buffer_8
  assign Adr7__0 = BLEQ ? 8'h20 : 8'bz;  // Controlled_Buffer controlled_buffer_9
  assign Adr7__0 = BLSSU ? 8'h21 : 8'bz;  // Controlled_Buffer controlled_buffer_10
  assign Adr7__0 = JLEQ ? 8'h22 : 8'bz;  // Controlled_Buffer controlled_buffer_11
  assign Adr7__0 = JMP ? 8'h23 : 8'bz;  // Controlled_Buffer controlled_buffer_12
  assign Adr7__0 = LD ? 8'h2a : 8'bz;  // Controlled_Buffer controlled_buffer_13
  assign Adr7__0 = JSR ? 8'h24 : 8'bz;  // Controlled_Buffer controlled_buffer_14
  assign Adr7__0 = ST ? 8'h2c : 8'bz;  // Controlled_Buffer controlled_buffer_15
  assign Adr7__0 = DEC ? 8'h33 : 8'bz;  // Controlled_Buffer controlled_buffer_16
  assign Adr7__0 = SUB ? 8'h35 : 8'bz;  // Controlled_Buffer controlled_buffer_17
  assign Adr7__0 = XOR ? 8'h37 : 8'bz;  // Controlled_Buffer controlled_buffer_18
  assign Adr7__0 = AND ? 8'h39 : 8'bz;  // Controlled_Buffer controlled_buffer_19
  assign Adr7__0 = STRFIND ? 8'h3b : 8'bz;  // Controlled_Buffer controlled_buffer_20
endmodule

module KMADR_ADDR (
  input  immed,
  input  memind,
  input  regdir,
  input  regind,
  input  predec,
  input  pcrelpom,
  output [4:0] Adr4__0
);

  assign Adr4__0 = immed ? 5'b00010 : 5'bz;  // Controlled_Buffer controlled_buffer_1
  assign Adr4__0 = memind ? 5'b00011 : 5'bz;  // Controlled_Buffer controlled_buffer_2
  assign Adr4__0 = regdir ? 5'b01110 : 5'bz;  // Controlled_Buffer controlled_buffer_3
  assign Adr4__0 = regind ? 5'b01111 : 5'bz;  // Controlled_Buffer controlled_buffer_4
  assign Adr4__0 = predec ? 5'b10000 : 5'bz;  // Controlled_Buffer controlled_buffer_5
  assign Adr4__0 = pcrelpom ? 5'b10100 : 5'bz;  // Controlled_Buffer controlled_buffer_6
endmodule

module ROM_EXEC (
  input  [6:0] A6__0,
  input  CS,
  output [31:0] DOUT31__0,
  output [12:0] DOUT44__32
);

  ROM #(.addrWidth(7), .dataWidth(13)) rom_1 (.addr(A6__0), .data(DOUT44__32), .sel(CS));
  ROM #(.addrWidth(7), .dataWidth(32)) rom_2 (.addr(A6__0), .data(DOUT31__0), .sel(CS));
endmodule

module ROM_ADDR (
  input  [5:0] A5__0,
  input  CS,
  output [30:0] DOUT30__0,
  output [5:0] DOUT36__31
);

  ROM #(.addrWidth(6), .dataWidth(6)) rom_1 (.addr(A5__0), .data(DOUT36__31), .sel(CS));
  ROM #(.addrWidth(6), .dataWidth(31)) rom_2 (.addr(A5__0), .data(DOUT30__0), .sel(CS));
endmodule

module ROM_INTR (
  input  [5:0] A5__0,
  input  CS,
  output [30:0] DOUT30__0,
  output [5:0] DOUT36__31
);

  ROM #(.addrWidth(6), .dataWidth(6)) rom_1 (.addr(A5__0), .data(DOUT36__31), .sel(CS));
  ROM #(.addrWidth(6), .dataWidth(31)) rom_2 (.addr(A5__0), .data(DOUT30__0), .sel(CS));
endmodule
