// Logisim project ORT2Project.circ as structural Verilog: 8 circuits, main circuit COMPUTER
module COMPUTER (
);

  wire BTN_RST_out, CLK, cpu_1_inta, interrupt_interface_8_1_p4, interrupt_interface_8_1_p5,
       interrupt_interface_8_1_p6, interrupt_interface_8_1_p7, interrupt_interface_8_1_p8,
       interrupt_interface_8_1_p9, interrupt_interface_8_1_p10, interrupt_interface_8_1_p11,
       pull_resistor_1_node, pull_resistor_5_node, ram_1_out_8, rst;
  wire [2:0] cpu_1_uext2_0;
  wire [7:0] interrupt_interface_8_1_p1, pull_resistor_3_node, ram_1_out_7;
  wire [15:0] pull_resistor_2_node;

  Button BTN_RST (.out(BTN_RST_out));
  Clock u_CLK (.out(CLK));
  // RisingEdge risingedge_1: pin names not known; wires that end beside it: BTN_RST_out, CLK, rst
  RAM ram_1 (
    .in_1(pull_resistor_2_node), .in_2(CLK), .in_3(pull_resistor_3_node), .in_4(pull_resistor_1_node),
    .in_5(pull_resistor_5_node), .in_6(rst), .out_7(ram_1_out_7), .out_8(ram_1_out_8));
  Pull_Resistor pull_resistor_1 (.node(pull_resistor_1_node));
  Pull_Resistor pull_resistor_2 (.node(pull_resistor_2_node));
  Pull_Resistor pull_resistor_3 (.node(pull_resistor_3_node));
  Pull_Resistor pull_resistor_4 (.node(ram_1_out_7));
  Pull_Resistor pull_resistor_5 (.node(pull_resistor_5_node));
  Pull_Resistor pull_resistor_6 (.node(ram_1_out_8));
  CPU cpu_1 (
    .in_1(rst), .in_2(CLK), .in_3(ram_1_out_8), .in_4(ram_1_out_7), .ABUS(pull_resistor_2_node),
    .DOUTBUS(pull_resistor_3_node), .out_8(pull_resistor_1_node), .out_9(pull_resistor_5_node),
    .inta(cpu_1_inta), .intr7__0(interrupt_interface_8_1_p1), .UEXT2_0(cpu_1_uext2_0));
  // INTERRUPT_INTERFACE_8 interrupt_interface_8_1: pin names not known; wires that end beside it: interrupt_interface_8_1_p1, cpu_1_inta, cpu_1_uext2_0, interrupt_interface_8_1_p4, interrupt_interface_8_1_p5, interrupt_interface_8_1_p6, interrupt_interface_8_1_p7, interrupt_interface_8_1_p8, interrupt_interface_8_1_p9, interrupt_interface_8_1_p10, interrupt_interface_8_1_p11, CLK
  Button BTN_INTR7 (.out(interrupt_interface_8_1_p4));
  Button BTN_INTR6 (.out(interrupt_interface_8_1_p5));
  Button BTN_INTR5 (.out(interrupt_interface_8_1_p6));
  Button BTN_INTR4 (.out(interrupt_interface_8_1_p7));
  Button BTN_INTR3 (.out(interrupt_interface_8_1_p8));
  Button BTN_INTR2 (.out(interrupt_interface_8_1_p9));
  Button BTN_INTR1 (.out(interrupt_interface_8_1_p10));
  Button BTN_INTR0 (.out(interrupt_interface_8_1_p11));
endmodule

module CPU (
  input  in_1,
  input  in_2,
  input  in_3,
  input  [7:0] in_4,
  input  [7:0] intr7__0,
  output [15:0] ABUS,
  output [7:0] DOUTBUS,
  output out_8,
  output out_9,
  output inta,
  output [2:0] UEXT2_0
);

  wire [3:0] common_1_phaseffbus;
  wire [5:0] common_1_addrbus;
  wire [6:0] pull_resistor_1_node;
  wire [7:0] DW7__0, DW15__8, pull_resistor_5_node;
  wire [11:0] pull_resistor_4_node;
  wire [14:0] pull_resistor_6_node;
  wire [15:0] A, B, INTRADDR, PSW, SUB15__0;
  wire [20:0] common_1_instrucbus;

  COMMON common_1 (
    .CLK(in_2), .RST(in_1), .DIN(in_4), .CMEMBUS(pull_resistor_6_node), .MAR(ABUS), .MDR(DOUTBUS),
    .PHASEFFBUS(common_1_phaseffbus), .INSTRUCBUS(common_1_instrucbus), .ADDRBUS(common_1_addrbus),
    .PSW(PSW), .CREGBUS(pull_resistor_4_node), .CFFBUS(pull_resistor_5_node), .B(B), .A(A),
    .CPSW(pull_resistor_1_node), .IVTPPDSP(INTRADDR), .DWH(DW15__8), .DWL(DW7__0), .SUB15__0(SUB15__0));
  Pull_Resistor pull_resistor_1 (.node(pull_resistor_1_node));
  Pull_Resistor pull_resistor_2 (.node(common_1_instrucbus));
  Pull_Resistor pull_resistor_3 (.node(common_1_phaseffbus));
  Pull_Resistor pull_resistor_4 (.node(pull_resistor_4_node));
  Pull_Resistor pull_resistor_5 (.node(pull_resistor_5_node));
  Pull_Resistor pull_resistor_6 (.node(pull_resistor_6_node));
  Pull_Resistor pull_resistor_7 (.node(common_1_addrbus));
  FETCH fetch_1 (
    .in_1(in_1), .in_2(in_2), .in_3(in_3), .PHASEFFBUS(common_1_phaseffbus),
    .INSTRUCBUS(common_1_instrucbus), .ADDRBUS(common_1_addrbus), .PSW(PSW), .rdMEM(out_9),
    .CMEMBUS(pull_resistor_6_node), .CFFBUS(pull_resistor_5_node), .CREGBUS(pull_resistor_4_node));
  ADDR addr_1 (
    .in_1(in_1), .in_2(in_2), .in_3(in_3), .PHASEFFBUS(common_1_phaseffbus),
    .INSTRUCBUS(common_1_instrucbus), .ADDRBUS(common_1_addrbus), .rdMEM(out_9),
    .CMEMBUS(pull_resistor_6_node), .CFFBUS(pull_resistor_5_node), .CREGBUS(pull_resistor_4_node));
  EXEC exec_1 (
    .in_3(in_1), .in_4(in_2), .in_5(in_3), .B(B), .PHASEFFBUS(common_1_phaseffbus),
    .INSTRUCBUS(common_1_instrucbus), .ADDRBUS(common_1_addrbus), .PSW(PSW), .A(A),
    .CMEMBUS(pull_resistor_6_node), .CFFBUS(pull_resistor_5_node), .CREGBUS(pull_resistor_4_node),
    .CPSW(pull_resistor_1_node), .rdMEM(out_9), .wrMEM(out_8), .DWH(DW15__8), .DWL(DW7__0),
    .SUB15__0(SUB15__0), .in_11(DOUTBUS));
  INTR intr_1 (
    .in_1(in_1), .in_2(in_2), .in_3(in_3), .PHASEFFBUS(common_1_phaseffbus),
    .INSTRUCBUS(common_1_instrucbus), .PSW(PSW), .intr(intr7__0), .ADDIVTP(INTRADDR),
    .CMEMBUS(pull_resistor_6_node), .CFFBUS(pull_resistor_5_node), .CREGBUS(pull_resistor_4_node),
    .rdMEM(out_9), .wrMEM(out_8), .UEXT2__0(UEXT2_0), .inta(inta));

  // Other names for the same wires on the sheet: CLK = in_2; DIN7__0[7:0] = in_4; FCBUS = in_3; MAR[15:0] = ABUS;
  //   MDR[7:0] = DOUTBUS; RD = out_9; rst = in_1; UEXT2__0[2:0] = UEXT2_0; WR = out_8
endmodule

module COMMON (
  input  CLK,
  input  RST,
  input  [7:0] DIN,
  input  [15:0] A,
  input  [15:0] IVTPPDSP,
  input  [14:0] CMEMBUS,
  input  [7:0] CFFBUS,
  input  [11:0] CREGBUS,
  input  [6:0] CPSW,
  input  [15:0] SUB15__0,
  output [7:0] DWH,
  output [7:0] DWL,
  output [15:0] MAR,
  output [7:0] MDR,
  output [3:0] PHASEFFBUS,
  output [20:0] INSTRUCBUS,
  output [5:0] ADDRBUS,
  output [15:0] PSW,
  output [15:0] B
);

  wire adrinst, ADRINSTR, and_1_out, and_2_out, and_3_out, and_4_out, and_5_out, and_6_out, and_7_out,
       and_8_out, and_9_out, and_10_out, and_11_out, and_12_out, and_13_out, and_14_out, and_15_out,
       and_16_out, and_17_out, and_18_out, and_19_out, and_20_out, and_21_out, and_22_out, and_23_out,
       and_24_out, and_25_out, and_26_out, and_27_out, and_28_out, and_29_out, and_30_out, and_32_out,
       bezadrinst, branchinst, jmpinst, mp2_16b_1_p3, mp4_16b_1_p5, mp4_16b_2_p5, mp8_8b_1_p8, mp8_16b_1_p8,
       nepadr, nepadrinst, nepbezadrinst, nepbranchinst, nepinst, nepjmpinst, not_1_out, not_5_out,
       not_9_out, or_2_out, or_4_out, or_5_out, or_6_out, or_7_out, or_8_out, or_9_out, or_10_out, or_11_out,
       or_12_out, reg16_inc_ld_2_p4, rsff_2_p4, rsff_3_p4, rsff_4_p4, rsff_6_p4, rsff_7_p4, rsff_8_p3,
       rsff_8_p4, rsff_9_p3, rsff_10_p4;
  wire [3:0] IR27__24;
  wire [7:0] IR7__0, IR15__8, IR23__16;
  wire [7:4] IR31__24;
  wire [15:0] ADDIREG15__0, ADDPCREL15__0, GPR15__0, mp2_16b_2_p3, PC15__0, SP15__0;

  // REG8_LD reg8_ld_1: pin names not known; wires that end beside it: CLK, MDR, {IR31__24, IR27__24}, CREGBUS[8]
  // MP8_16b mp8_16b_1: pin names not known; wires that end beside it: CMEMBUS[14], CMEMBUS[6], CMEMBUS[5], PC15__0, {IR15__8, IR7__0}, GPR15__0, SP15__0, mp8_16b_1_p8, B, {DWH, DWL}, ADDPCREL15__0, IVTPPDSP, 1'b1
  // REG16_INC_LD reg16_inc_ld_1: pin names not known; wires that end beside it: CLK, mp8_16b_1_p8, MAR, CMEMBUS[0], CMEMBUS[1]
  // REG8_LD reg8_ld_2: pin names not known; wires that end beside it: CLK, MDR, IR23__16, CREGBUS[7]
  // DC4_16 dc4_16_1: pin names not known; wires that end beside it: IR31__24, PSW[0], bezadrinst, branchinst, jmpinst, adrinst, nepinst, nepinst, nepinst, nepinst, nepinst, nepinst, nepinst, nepinst, nepinst, nepinst, nepinst, nepinst
  // DC4_16 dc4_16_2: pin names not known; wires that end beside it: IR27__24, branchinst, INSTRUCBUS[6], INSTRUCBUS[7], INSTRUCBUS[8], INSTRUCBUS[9], INSTRUCBUS[10], nepbranchinst, nepbranchinst, nepbranchinst, nepbranchinst, nepbranchinst, nepbranchinst, nepbranchinst, nepbranchinst, nepbranchinst, nepbranchinst, nepbranchinst
  // MP4_16b mp4_16b_1: pin names not known; wires that end beside it: CREGBUS[3], CREGBUS[2], {DWH, DWL}, {IR15__8, IR7__0}, mp4_16b_1_p5, GPR15__0, 1'b1
  // REG16 reg16_1: pin names not known; wires that end beside it: CLK, mp4_16b_1_p5, B, CREGBUS[1], CREGBUS[11]
  // ADD16 add16_1: pin names not known; wires that end beside it: {{9{IR23__16[7]}}, IR23__16[6:0]}, ADDIREG15__0, PC15__0
  // REG8_LD reg8_ld_3: pin names not known; wires that end beside it: CLK, MDR, IR15__8, CREGBUS[6]
  or or_1 (INSTRUCBUS[20], and_1_out, or_2_out);
  // DC4_16 dc4_16_3: pin names not known; wires that end beside it: IR27__24, bezadrinst, INSTRUCBUS[0], INSTRUCBUS[1], INSTRUCBUS[2], INSTRUCBUS[3], INSTRUCBUS[4], INSTRUCBUS[5], nepbezadrinst, nepbezadrinst, nepbezadrinst, nepbezadrinst, nepbezadrinst, nepbezadrinst, nepbezadrinst, nepbezadrinst, nepbezadrinst, nepbezadrinst
  // DC4_16 dc4_16_4: pin names not known; wires that end beside it: IR27__24, jmpinst, INSTRUCBUS[11], INSTRUCBUS[12], nepjmpinst, nepjmpinst, nepjmpinst, nepjmpinst, nepjmpinst, nepjmpinst, nepjmpinst, nepjmpinst, nepjmpinst, nepjmpinst, nepjmpinst, nepjmpinst, nepjmpinst, nepjmpinst
  and and_1 (and_1_out, INSTRUCBUS[14], ADDRBUS[0]);
  or or_2 (or_2_out, and_2_out, and_3_out, and_4_out, and_5_out, and_6_out, nepinst);
  // REG8_LD reg8_ld_4: pin names not known; wires that end beside it: CLK, MDR, DWH, CREGBUS[10]
  // ADD16 add16_2: pin names not known; wires that end beside it: {{9{IR15__8[7]}}, IR15__8[6:0]}, ADDPCREL15__0, PC15__0
  // MP8_8b mp8_8b_1: pin names not known; wires that end beside it: CMEMBUS[9], CMEMBUS[8], CMEMBUS[7], DIN, PC15__0[15:8], PC15__0[7:0], A[15:8], mp8_8b_1_p8, A[7:0], PSW[15:8], PSW[7:0], 1'b1
  // REG8_LD reg8_ld_5: pin names not known; wires that end beside it: CLK, mp8_8b_1_p8, MDR, CMEMBUS[2]
  // REG8_LD reg8_ld_6: pin names not known; wires that end beside it: CLK, MDR, IR7__0, CREGBUS[5]
  // REG8_LD reg8_ld_7: pin names not known; wires that end beside it: CLK, MDR, DWL, CREGBUS[9]
  // MP4_16b mp4_16b_2: pin names not known; wires that end beside it: CMEMBUS[12], CMEMBUS[13], {IR23__16, IR15__8}, ADDPCREL15__0, mp4_16b_2_p5, {DWH, DWL}, ADDIREG15__0, 1'b1
  // DC3_8 dc3_8_1: pin names not known; wires that end beside it: IR27__24[2:0], adrinst, INSTRUCBUS[13], INSTRUCBUS[14], INSTRUCBUS[15], INSTRUCBUS[16], INSTRUCBUS[17], INSTRUCBUS[18], INSTRUCBUS[19], nepadr
  // DC3_8 dc3_8_2: pin names not known; wires that end beside it: IR23__16[6:4], adrinst, ADDRBUS[0], ADDRBUS[1], ADDRBUS[2], ADDRBUS[3], nepadrinst, ADDRBUS[4], ADDRBUS[5], nepadrinst
  and and_2 (and_2_out, bezadrinst, nepbezadrinst);
  and and_3 (and_3_out, jmpinst, nepjmpinst);
  and and_4 (and_4_out, branchinst, nepbranchinst);
  and and_5 (and_5_out, adrinst, nepadrinst);
  and and_6 (and_6_out, adrinst, nepadr);
  // REG16 reg16_2: pin names not known; wires that end beside it: CLK, 16'hf000, SP15__0, RST, CMEMBUS[10], CMEMBUS[11]
  not not_1 (not_1_out, RST);
  // RSFF rsff_1: pin names not known; wires that end beside it: CFFBUS[1], CLK, CFFBUS[0], not_1_out, PHASEFFBUS[0]
  // MP2_16b mp2_16b_1: pin names not known; wires that end beside it: RST, mp4_16b_2_p5, mp2_16b_1_p3, 16'h1000, 1'b1
  // REG16_INC_LD reg16_inc_ld_2: pin names not known; wires that end beside it: CLK, mp2_16b_1_p3, PC15__0, reg16_inc_ld_2_p4, CMEMBUS[4]
  or or_3 (reg16_inc_ld_2_p4, CMEMBUS[3], RST);
  // RSFF rsff_2: pin names not known; wires that end beside it: CFFBUS[3], CLK, CFFBUS[2], rsff_2_p4, PHASEFFBUS[1]
  not not_2 (rsff_2_p4, RST);
  and and_7 (and_7_out, ~SUB15__0[15], ~B[15], A[15]);  // AND_Gate
  and and_8 (and_8_out, SUB15__0[15], B[15], ~A[15]);  // AND_Gate
  and and_9 (and_9_out, ~A[0], ~A[1], ~A[2], ~A[3], ~A[4], ~A[5], ~A[6], ~A[7], ~A[8], ~A[9], ~A[10], ~A[11], ~A[12], ~A[13], ~A[14], ~A[15]);  // AND_Gate
  or or_4 (or_4_out, INSTRUCBUS[16], INSTRUCBUS[15]);
  and and_10 (and_10_out, ~SUB15__0[15], ~B[15], A[15]);  // AND_Gate
  or or_5 (or_5_out, and_10_out, and_11_out);
  and and_11 (and_11_out, SUB15__0[15], B[15], ~A[15]);  // AND_Gate
  and and_12 (and_12_out, MDR[4], INSTRUCBUS[2]);
  and and_13 (and_13_out, INSTRUCBUS[3], A[0]);
  and and_14 (and_14_out, or_6_out, or_7_out);
  or or_6 (or_6_out, INSTRUCBUS[16], INSTRUCBUS[15]);
  or or_7 (or_7_out, and_7_out, and_8_out);
  // RSFF rsff_3: pin names not known; wires that end beside it: CFFBUS[5], CLK, CFFBUS[4], rsff_3_p4, PHASEFFBUS[2]
  not not_3 (rsff_3_p4, RST);
  and and_15 (and_15_out, MDR[1], INSTRUCBUS[2]);
  and and_16 (and_16_out, ADRINSTR, and_9_out);
  and and_17 (and_17_out, MDR[2], INSTRUCBUS[2]);
  and and_18 (and_18_out, ADRINSTR, A[15]);
  and and_19 (and_19_out, MDR[3], INSTRUCBUS[2]);
  and and_20 (and_20_out, or_4_out, or_5_out);
  or or_8 (or_8_out, and_12_out, and_13_out, and_14_out);
  or or_9 (or_9_out, and_15_out, and_16_out);
  or or_10 (or_10_out, and_17_out, and_18_out);
  or or_11 (or_11_out, and_19_out, and_20_out);
  and and_21 (and_21_out, MDR[7], INSTRUCBUS[2]);
  // MP2_16b mp2_16b_2: pin names not known; wires that end beside it: CREGBUS[0], A, mp2_16b_2_p3, B, 1'b1
  GPR16X16 gpr16x16_1 (.DI15__0(mp2_16b_2_p3), .A3__0(IR23__16[3:0]), .WR(CREGBUS[4]), .CLK(CLK), .DO15__0(GPR15__0));
  and and_22 (and_22_out, ~MDR[0], INSTRUCBUS[2], CPSW[5]);  // AND_Gate
  or or_12 (or_12_out, and_22_out, CPSW[0]);
  and and_23 (and_23_out, MDR[0], INSTRUCBUS[2], CPSW[5]);
  and and_24 (and_24_out, ~or_9_out, CPSW[4]);  // AND_Gate
  and and_25 (and_25_out, or_9_out, CPSW[4]);
  and and_26 (and_26_out, ~or_10_out, CPSW[3]);  // AND_Gate
  and and_27 (and_27_out, or_10_out, CPSW[3]);
  and and_28 (and_28_out, ~or_8_out, CPSW[6]);  // AND_Gate
  and and_29 (and_29_out, or_8_out, CPSW[6]);
  // RSFF rsff_4: pin names not known; wires that end beside it: CFFBUS[7], CLK, CFFBUS[6], rsff_4_p4, PHASEFFBUS[3]
  not not_4 (rsff_4_p4, RST);
  or or_13 (ADRINSTR, INSTRUCBUS[17], INSTRUCBUS[18], INSTRUCBUS[13], INSTRUCBUS[18], INSTRUCBUS[16], INSTRUCBUS[15]);
  not not_5 (not_5_out, RST);
  // RSFF rsff_5: pin names not known; wires that end beside it: or_12_out, CLK, and_23_out, not_5_out, PSW[0]
  // RSFF rsff_6: pin names not known; wires that end beside it: and_24_out, CLK, and_25_out, rsff_6_p4, PSW[1]
  not not_6 (rsff_6_p4, RST);
  // RSFF rsff_7: pin names not known; wires that end beside it: and_26_out, CLK, and_27_out, rsff_7_p4, PSW[2]
  not not_7 (rsff_7_p4, RST);
  and and_30 (and_30_out, ~or_11_out, CPSW[2]);  // AND_Gate
  // RSFF rsff_8: pin names not known; wires that end beside it: and_30_out, CLK, rsff_8_p3, rsff_8_p4, PSW[3]
  not not_8 (rsff_8_p4, RST);
  and and_31 (rsff_8_p3, or_11_out, CPSW[2]);
  not not_9 (not_9_out, RST);
  and and_32 (and_32_out, ~and_21_out, CPSW[1]);  // AND_Gate
  // RSFF rsff_9: pin names not known; wires that end beside it: and_32_out, CLK, rsff_9_p3, not_9_out, PSW[15]
  and and_33 (rsff_9_p3, and_21_out, CPSW[1]);
  // RSFF rsff_10: pin names not known; wires that end beside it: and_28_out, CLK, and_29_out, rsff_10_p4, PSW[4]
  not not_10 (rsff_10_p4, RST);

  // Other names for the same wires on the sheet: A15__0[15:0] = A; immed = ADDRBUS[0]; memind = ADDRBUS[1];
  //   regdir = ADDRBUS[2]; regind = ADDRBUS[3]; predec = ADDRBUS[4]; pcrelpom = ADDRBUS[5]; B15__0[15:0] = B;
  //   stFETCH = CFFBUS[0]; clFETCH = CFFBUS[1]; stADDR = CFFBUS[2]; clADDR = CFFBUS[3]; stEXEC = CFFBUS[4];
  //   clEXEC = CFFBUS[5]; stINTR = CFFBUS[6]; clINTR = CFFBUS[7]; ldMAR = CMEMBUS[0]; incMAR = CMEMBUS[1];
  //   ldMDR = CMEMBUS[2]; ldPC = CMEMBUS[3]; incPC = CMEMBUS[4]; mxMAR0 = CMEMBUS[5]; mxMAR1 = CMEMBUS[6];
  //   mxMDR0 = CMEMBUS[7]; mxMDR1 = CMEMBUS[8]; mxMDR2 = CMEMBUS[9]; incSP = CMEMBUS[10]; decSP = CMEMBUS[11];
  //   mxPC1 = CMEMBUS[12]; mxPC0 = CMEMBUS[13]; mxMAR2 = CMEMBUS[14]; clPSWSTART = CPSW[0]; ldI = CPSW[1];
  //   ldV = CPSW[2]; ldN = CPSW[3]; ldZ = CPSW[4]; ldSTART = CPSW[5]; ldC = CPSW[6]; mxGPR0 = CREGBUS[0];
  //   ldB = CREGBUS[1]; mxB0 = CREGBUS[2]; mxB1 = CREGBUS[3]; wrGPR = CREGBUS[4]; ldIR7__0 = CREGBUS[5];
  //   ldIR15__8 = CREGBUS[6]; ldIR23__16 = CREGBUS[7]; ldIR31__24 = CREGBUS[8]; ldDWL = CREGBUS[9];
  //   ldDWH = CREGBUS[10]; decB = CREGBUS[11]; Din7__0[7:0] = DIN; ENTRADDR15__0[15:0] = IVTPPDSP;
  //   HALT = INSTRUCBUS[0]; RTS = INSTRUCBUS[1]; RTI = INSTRUCBUS[2]; ROR = INSTRUCBUS[3]; PUSH = INSTRUCBUS[4];
  //   POP = INSTRUCBUS[5]; BOVF = INSTRUCBUS[6]; BNCR = INSTRUCBUS[7]; BLEQ = INSTRUCBUS[8]; BLSSU = INSTRUCBUS[9];
  //   JLEQ = INSTRUCBUS[10]; JMP = INSTRUCBUS[11]; JSR = INSTRUCBUS[12]; LD = INSTRUCBUS[13]; ST = INSTRUCBUS[14];
  //   DEC = INSTRUCBUS[15]; SUB = INSTRUCBUS[16]; XOR = INSTRUCBUS[17]; AND = INSTRUCBUS[18];
  //   STRFIND = INSTRUCBUS[19]; grinst = INSTRUCBUS[20]; IR31__24[3:0] = IR27__24; MAR15__0[15:0] = MAR;
  //   MDR7__0[7:0] = MDR; FETCH = PHASEFFBUS[0]; ADDR = PHASEFFBUS[1]; EXEC = PHASEFFBUS[2]; INTR = PHASEFFBUS[3];
  //   PSW15__0[15:0] = PSW; PSWSTART = PSW[0]; PSWZ = PSW[1]; PSWN = PSW[2]; PSWV = PSW[3]; PSWC = PSW[4];
  //   PSWI = PSW[15]; SUB15 = SUB15__0[15]

  // Notes on the sheet:
  //   Sabirac
  //   MAR
  //   Instrukcijski registar
  //   Pomocni registri
  //   Dekoderi za prepoznavanje instrukcije
  //   MDR
  //   PC
  //   SP
  //   Dekoderi za prepoznavanje nacina adresiranja
  //   FF za pokretanje FETCH, ADDR, EXEC i INTR faze izvršavanja instrukcije
  //   Registarski fajl
  //   Programska statusna reč (PSW)
endmodule

module FETCH (
  input  in_1,
  input  in_2,
  input  in_3,
  input  [3:0] PHASEFFBUS,
  input  [20:0] INSTRUCBUS,
  input  [5:0] ADDRBUS,
  input  [15:0] PSW,
  output [14:0] CMEMBUS,
  output [7:0] CFFBUS,
  output [11:0] CREGBUS,
  output rdMEM
);

  wire addr2, addr3, addr4, addr_t, and_1_out, and_2_out, and_3_out, and_4_out, and_5_out, and_6_out,
       and_10_out, and_11_out, bezadr1, bradr2, bradr3, brbezadr1, brcnd, brgrinst, brjmp2, brjmp3,
       brnotfcbus, bruncnd, clFETCH, incPC, jmp2, jmp3, ldIR7__0, ldIR15__8, ldIR23__16, ldIR31__24, ldMAR,
       ldMDR, not_1_out, not_3_out, not_4_out, not_5_out, notPSWSTandFETCH, or_6_out, or_7_out, or_8_out,
       rdMEM_t, reg5_cl_inc_ld_1_p5, reg5_cl_inc_ld_1_p6, stADDR, stEXEC;
  wire [3:0] dc4_16_1_p1;
  wire [4:0] reg5_cl_inc_ld_1_p3, reg5_cl_inc_ld_1_p4;
  wire [30:20] rom64x37_1_p3;

  or or_1 (jmp2, INSTRUCBUS[6], INSTRUCBUS[7], INSTRUCBUS[8], INSTRUCBUS[9]);
  or or_2 (bezadr1, INSTRUCBUS[1], INSTRUCBUS[3], INSTRUCBUS[4], INSTRUCBUS[2], INSTRUCBUS[5], INSTRUCBUS[0]);
  not not_1 (not_1_out, in_1);
  // REG5_CL_INC_LD reg5_cl_inc_ld_1: pin names not known; wires that end beside it: in_2, not_1_out, reg5_cl_inc_ld_1_p3, reg5_cl_inc_ld_1_p4, reg5_cl_inc_ld_1_p5, reg5_cl_inc_ld_1_p6
  not not_2 (reg5_cl_inc_ld_1_p6, reg5_cl_inc_ld_1_p5);
  // DC4_16 dc4_16_1: pin names not known; wires that end beside it: dc4_16_1_p1, 1'b1, brjmp3, bruncnd, notPSWSTandFETCH, brbezadr1, brjmp2, bradr2, bradr3, brnotfcbus, brgrinst
  or or_3 (reg5_cl_inc_ld_1_p5, bruncnd, brcnd);
  // ROM64x37 rom64x37_1: pin names not known; wires that end beside it: {1'b0, reg5_cl_inc_ld_1_p4}, 1'b1, {rom64x37_1_p3, reg5_cl_inc_ld_1_p3, dc4_16_1_p1, stEXEC, stADDR, clFETCH, ldIR7__0, ldIR15__8, ldIR23__16, ldIR31__24, ldMDR, rdMEM_t, incPC, ldMAR}
  or or_4 (addr_t, INSTRUCBUS[17], INSTRUCBUS[13], INSTRUCBUS[14], INSTRUCBUS[18], INSTRUCBUS[15], INSTRUCBUS[16], INSTRUCBUS[19]);
  or or_5 (jmp3, INSTRUCBUS[10], INSTRUCBUS[11], INSTRUCBUS[12]);
  not not_3 (not_3_out, PHASEFFBUS[0]);
  not not_4 (not_4_out, PSW[0]);
  or or_6 (or_6_out, ADDRBUS[3], ADDRBUS[2], ADDRBUS[4]);
  or or_7 (or_7_out, not_3_out, not_4_out);
  not not_5 (not_5_out, in_3);
  or or_8 (or_8_out, ADDRBUS[0], ADDRBUS[1]);
  and and_1 (and_1_out, or_7_out, notPSWSTandFETCH);
  and and_2 (and_2_out, brbezadr1, bezadr1);
  and and_3 (and_3_out, brjmp2, jmp2);
  and and_4 (and_4_out, bradr2, addr2);
  and and_5 (and_5_out, brjmp3, jmp3);
  and and_6 (and_6_out, brnotfcbus, not_5_out);
  and and_7 (addr4, addr_t, or_8_out);
  and and_8 (addr2, addr_t, or_6_out);
  and and_9 (addr3, addr_t, ADDRBUS[5]);
  and and_10 (and_10_out, bradr3, addr3);
  and and_11 (and_11_out, INSTRUCBUS[20], brgrinst);
  or or_9 (brcnd, and_10_out, and_1_out, and_2_out, and_3_out, and_4_out, and_5_out, and_6_out, and_11_out);
  assign CMEMBUS[0] = ldMAR ? 1'b1 : 1'bz;  // Controlled_Buffer controlled_buffer_1
  assign CMEMBUS[2] = ldMDR ? 1'b1 : 1'bz;  // Controlled_Buffer controlled_buffer_2
  assign CMEMBUS[4] = incPC ? 1'b1 : 1'bz;  // Controlled_Buffer controlled_buffer_3
  assign CFFBUS[1] = clFETCH ? 1'b1 : 1'bz;  // Controlled_Buffer controlled_buffer_4
  assign CFFBUS[2] = stADDR ? 1'b1 : 1'bz;  // Controlled_Buffer controlled_buffer_5
  assign CFFBUS[4] = stEXEC ? 1'b1 : 1'bz;  // Controlled_Buffer controlled_buffer_6
  assign CREGBUS[5] = ldIR7__0 ? 1'b1 : 1'bz;  // Controlled_Buffer controlled_buffer_7
  assign CREGBUS[6] = ldIR15__8 ? 1'b1 : 1'bz;  // Controlled_Buffer controlled_buffer_8
  assign CREGBUS[7] = ldIR23__16 ? 1'b1 : 1'bz;  // Controlled_Buffer controlled_buffer_9
  assign CREGBUS[8] = ldIR31__24 ? 1'b1 : 1'bz;  // Controlled_Buffer controlled_buffer_10
  assign rdMEM = rdMEM_t ? 1'b1 : 1'bz;  // Controlled_Buffer controlled_buffer_11

  // Other names for the same wires on the sheet: immed = ADDRBUS[0]; memind = ADDRBUS[1]; regdir = ADDRBUS[2];
  //   regind = ADDRBUS[3]; predec = ADDRBUS[4]; pcrelpom = ADDRBUS[5]; CLK = in_2; FCBUS = in_3; HALT = INSTRUCBUS[0];
  //   RTS = INSTRUCBUS[1]; RTI = INSTRUCBUS[2]; ROR = INSTRUCBUS[3]; PUSH = INSTRUCBUS[4]; POP = INSTRUCBUS[5];
  //   BOVF = INSTRUCBUS[6]; BNCR = INSTRUCBUS[7]; BLEQ = INSTRUCBUS[8]; BLSSU = INSTRUCBUS[9]; JLEQ = INSTRUCBUS[10];
  //   JMP = INSTRUCBUS[11]; JSR = INSTRUCBUS[12]; LD = INSTRUCBUS[13]; ST = INSTRUCBUS[14]; DEC = INSTRUCBUS[15];
  //   SUB = INSTRUCBUS[16]; XOR = INSTRUCBUS[17]; AND = INSTRUCBUS[18]; STRFIND = INSTRUCBUS[19];
  //   grinst = INSTRUCBUS[20]; FETCH = PHASEFFBUS[0]; ADDR = PHASEFFBUS[1]; EXEC = PHASEFFBUS[2];
  //   INTR = PHASEFFBUS[3]; PSWSTART = PSW[0]; rst = in_1

  // Notes on the sheet:
  //   Operaciona jedinica
  //   Kontrolna jedinica
endmodule

module ADDR (
  input  in_1,
  input  in_2,
  input  in_3,
  input  [3:0] PHASEFFBUS,
  input  [20:0] INSTRUCBUS,
  input  [5:0] ADDRBUS,
  output [14:0] CMEMBUS,
  output [7:0] CFFBUS,
  output [11:0] CREGBUS,
  output rdMEM
);

  wire and_1_out, and_2_out, bradr, brcnd, brnotADDR, brnotfcbus, bruncnd, clADDR, decB, incMAR, ldB, ldDWH,
       ldDWL, ldMAR, ldMDR, mxB0, mxB1, mxGPR0, mxMAR0, mxMAR1, mxMAR2, not_1_out, not_3_out, not_4_out,
       rdMEM_t, reg5_cl_inc_ld_1_p5, reg5_cl_inc_ld_1_p6, stEXEC, wrGPR;
  wire [4:0] kmadr_addr_1_adr4__0, mp2_8b_1_p2, reg5_cl_inc_ld_1_p4;
  wire [7:0] mp2_8b_1_p3;
  wire [30:17] rom_addr_1_dout30__0;

  not not_1 (not_1_out, in_1);
  KMADR_ADDR kmadr_addr_1 (
    .immed(ADDRBUS[0]), .memind(ADDRBUS[1]), .regdir(ADDRBUS[2]), .regind(ADDRBUS[3]), .predec(ADDRBUS[4]),
    .pcrelpom(ADDRBUS[5]), .Adr4__0(kmadr_addr_1_adr4__0));
  // MP2_8b mp2_8b_1: pin names not known; wires that end beside it: bradr, {3'b000, mp2_8b_1_p2}, mp2_8b_1_p3, {3'b000, kmadr_addr_1_adr4__0}, mp2_8b_1_p3[7:5]
  // REG5_CL_INC_LD reg5_cl_inc_ld_1: pin names not known; wires that end beside it: in_2, not_1_out, mp2_8b_1_p3[4:0], reg5_cl_inc_ld_1_p4, reg5_cl_inc_ld_1_p5, reg5_cl_inc_ld_1_p6
  not not_2 (reg5_cl_inc_ld_1_p6, reg5_cl_inc_ld_1_p5);
  ROM_ADDR rom_addr_1 (
    .A5__0({1'b0, reg5_cl_inc_ld_1_p4}), .CS(1'b1),
    .DOUT30__0({rom_addr_1_dout30__0[30:25], mp2_8b_1_p2, rom_addr_1_dout30__0[19:17], decB, mxGPR0, wrGPR, incMAR, mxMAR2, ldDWL, ldDWH, stEXEC, clADDR, ldMDR, rdMEM_t, mxMAR1, mxB1, mxMAR0, ldMAR, mxB0, ldB}));  // open: DOUT36__31
  or or_1 (reg5_cl_inc_ld_1_p5, bruncnd, brcnd, bradr);
  // DC3_8 dc3_8_1: pin names not known; wires that end beside it: rom_addr_1_dout30__0[19:17], 1'b1, bruncnd, brnotADDR, brnotfcbus, bradr
  not not_3 (not_3_out, PHASEFFBUS[1]);
  not not_4 (not_4_out, in_3);
  and and_1 (and_1_out, not_3_out, brnotADDR);
  and and_2 (and_2_out, brnotfcbus, not_4_out);
  or or_2 (brcnd, and_1_out, and_2_out);
  assign CMEMBUS[1] = incMAR ? 1'b1 : 1'bz;  // Controlled_Buffer controlled_buffer_1
  assign CMEMBUS[0] = ldMAR ? 1'b1 : 1'bz;  // Controlled_Buffer controlled_buffer_2
  assign CMEMBUS[2] = ldMDR ? 1'b1 : 1'bz;  // Controlled_Buffer controlled_buffer_3
  assign CMEMBUS[5] = mxMAR0 ? 1'b1 : 1'bz;  // Controlled_Buffer controlled_buffer_4
  assign CMEMBUS[6] = mxMAR1 ? 1'b1 : 1'bz;  // Controlled_Buffer controlled_buffer_5
  assign CFFBUS[3] = clADDR ? 1'b1 : 1'bz;  // Controlled_Buffer controlled_buffer_6
  assign CFFBUS[4] = stEXEC ? 1'b1 : 1'bz;  // Controlled_Buffer controlled_buffer_7
  assign CREGBUS[0] = mxGPR0 ? 1'b1 : 1'bz;  // Controlled_Buffer controlled_buffer_8
  assign CREGBUS[1] = ldB ? 1'b1 : 1'bz;  // Controlled_Buffer controlled_buffer_9
  assign CREGBUS[2] = mxB0 ? 1'b1 : 1'bz;  // Controlled_Buffer controlled_buffer_10
  assign CREGBUS[3] = mxB1 ? 1'b1 : 1'bz;  // Controlled_Buffer controlled_buffer_11
  assign CREGBUS[4] = wrGPR ? 1'b1 : 1'bz;  // Controlled_Buffer controlled_buffer_12
  assign CREGBUS[9] = ldDWL ? 1'b1 : 1'bz;  // Controlled_Buffer controlled_buffer_13
  assign CREGBUS[10] = ldDWH ? 1'b1 : 1'bz;  // Controlled_Buffer controlled_buffer_14
  assign CREGBUS[11] = decB ? 1'b1 : 1'bz;  // Controlled_Buffer controlled_buffer_15
  assign CMEMBUS[14] = mxMAR2 ? 1'b1 : 1'bz;  // Controlled_Buffer controlled_buffer_16
  assign rdMEM = rdMEM_t ? 1'b1 : 1'bz;  // Controlled_Buffer controlled_buffer_17

  // Other names for the same wires on the sheet: immed = ADDRBUS[0]; memind = ADDRBUS[1]; regdir = ADDRBUS[2];
  //   regind = ADDRBUS[3]; predec = ADDRBUS[4]; pcrelpom = ADDRBUS[5]; CLK = in_2; FCBUS = in_3; ADDR = PHASEFFBUS[1];
  //   rst = in_1

  // Notes on the sheet:
  //   Operaciona jedinica
  //   Upravljacka jedinica
endmodule

module EXEC (
  input  [7:0] DWH,
  input  [7:0] DWL,
  input  in_3,
  input  in_4,
  input  in_5,
  input  [15:0] B,
  input  [3:0] PHASEFFBUS,
  input  [20:0] INSTRUCBUS,
  input  [5:0] ADDRBUS,
  input  [15:0] PSW,
  input  [7:0] in_11,
  output [15:0] A,
  output [14:0] CMEMBUS,
  output [7:0] CFFBUS,
  output [11:0] CREGBUS,
  output [6:0] CPSW,
  output rdMEM,
  output wrMEM,
  output [15:0] SUB15__0
);

  wire and_1_out, and_2_out, and_3_out, and_4_out, and_5_out, and_14_out, and_15_out, and_16_out, and_25_out,
       brcnd, brimmed, brnotbrorjmp, brnotEXEC, brnotFCBUS, bropr, brorjmp, brregdir, bruncnd, clCNT, clEXEC,
       clPSWSTART, decSP, equal, incCNT, incMAR, incSP, ldA, ldC, ldDWH, ldDWL, ldI, ldMAR, ldMDR, ldN, ldPC,
       ldSTART, ldV, ldZ, mp2_8b_1_p3, mp2_16b_1_p3, mp8_16b_1_p8, mxA0, mxA1, mxA2, mxMAR0, mxMAR1, mxMAR2,
       mxMDR0, mxMDR1, mxMDR2, mxPC0, mxPC1, mxSUB0, not_1_out, not_2_out, not_4_out, not_5_out, not_6_out,
       or_3_out, or_4_out, R0, R1, R2, R3, R4, R5, R6, R7, R8, R9, R10, R11, R12, R13, R14, R15, RA0, RA1,
       RA2, RA3, RA4, RA5, RA6, RA7, RA8, RA9, RA10, RA11, RA12, RA13, RA14, RA15, rdMEM_t, reg8_inc_ld_1_p5,
       reg8_inc_ld_1_p6, stINTR, wrGPR, wrMEM_t, xor_17_out;
  wire [2:0] dc3_8_1_p1;
  wire [6:0] mp2_8b_1_p2, reg8_inc_ld_1_p4;
  wire [7:0] mp2_8b_1_p4;
  wire [7:7] reg8_inc_ld_1_p4_2;
  wire [15:0] counter, SUB15__0_t;

  // DC3_8 dc3_8_1: pin names not known; wires that end beside it: dc3_8_1_p1, 1'b1, bruncnd, brnotEXEC, brimmed, brregdir, brnotbrorjmp, brnotFCBUS, bropr
  // MP8_16b mp8_16b_1: pin names not known; wires that end beside it: mxA2, mxA1, mxA0, B, {A[0], A[15:1]}, {DWH, DWL}, {R15, R14, R13, R12, R11, R10, R9, R8, R7, R6, R5, R4, R3, R2, R1, R0}, mp8_16b_1_p8, SUB15__0_t, counter, {RA15, RA14, RA13, RA12, RA11, RA10, RA9, RA8, RA7, RA6, RA5, RA4, RA3, RA2, RA1, RA0}, 1'b1
  not not_1 (not_1_out, in_3);
  // REG16_LD reg16_ld_1: pin names not known; wires that end beside it: in_4, not_1_out, mp8_16b_1_p8, A, ldA
  not not_2 (not_2_out, in_3);
  // MP2_8b mp2_8b_1: pin names not known; wires that end beside it: bropr, {1'b0, mp2_8b_1_p2}, mp2_8b_1_p3, mp2_8b_1_p4, 1'b1
  // REG8_INC_LD reg8_inc_ld_1: pin names not known; wires that end beside it: in_4, not_2_out, mp2_8b_1_p3, {reg8_inc_ld_1_p4_2[7], reg8_inc_ld_1_p4}, reg8_inc_ld_1_p5, reg8_inc_ld_1_p6
  not not_3 (reg8_inc_ld_1_p6, reg8_inc_ld_1_p5);
  KMOPREXEC kmoprexec_1 (
    .HALT(INSTRUCBUS[0]), .RTS(INSTRUCBUS[1]), .RTI(INSTRUCBUS[2]), .ROR(INSTRUCBUS[3]),
    .PUSH(INSTRUCBUS[4]), .POP(INSTRUCBUS[5]), .BOVF(INSTRUCBUS[6]), .BNCR(INSTRUCBUS[7]),
    .BLEQ(INSTRUCBUS[8]), .BLSSU(INSTRUCBUS[9]), .JLEQ(INSTRUCBUS[10]), .JMP(INSTRUCBUS[11]),
    .JSR(INSTRUCBUS[12]), .LD(INSTRUCBUS[13]), .ST(INSTRUCBUS[14]), .DEC(INSTRUCBUS[15]),
    .SUB(INSTRUCBUS[16]), .XOR(INSTRUCBUS[17]), .AND(INSTRUCBUS[18]), .STRFIND(INSTRUCBUS[19]),
    .Adr7__0(mp2_8b_1_p4));
  or or_1 (reg8_inc_ld_1_p5, bruncnd, brcnd, bropr);
  ROM_EXEC rom_exec_1 (
    .A6__0(reg8_inc_ld_1_p4), .CS(1'b1), .DOUT44__32({mp2_8b_1_p2, dc3_8_1_p1, clEXEC, stINTR, clPSWSTART}),
    .DOUT31__0({ldSTART, ldI, incCNT, mxPC1, ldDWH, ldDWL, rdMEM_t, incSP, mxMDR2, mxMDR1, decSP, mxSUB0, incMAR, ldMAR, mxMAR2, mxMAR1, mxMAR0, ldPC, mxPC0, ldV, clCNT, mxA2, mxA1, mxA0, wrGPR, wrMEM_t, ldMDR, mxMDR0, ldC, ldZ, ldN, ldA}));
  // MP2_16b mp2_16b_1: pin names not known; wires that end beside it: mxSUB0, B, mp2_16b_1_p3, 16'h1, 1'b1
  // SUB16 sub16_1: pin names not known; wires that end beside it: A, SUB15__0_t, mp2_16b_1_p3, 1'b0
  // REG16 reg16_1: pin names not known; wires that end beside it: clCNT, in_4, counter, incCNT
  xor xor_1 (R0, B[0], A[0]);
  xor xor_2 (R1, B[1], A[1]);
  xor xor_3 (R2, B[2], A[2]);
  xor xor_4 (R3, B[3], A[3]);
  xor xor_5 (R4, B[4], A[4]);
  xor xor_6 (R5, B[5], A[5]);
  xor xor_7 (R6, B[6], A[6]);
  xor xor_8 (R7, B[7], A[7]);
  not not_4 (not_4_out, PHASEFFBUS[2]);
  not not_5 (not_5_out, brorjmp);
  not not_6 (not_6_out, in_5);
  xor xor_9 (R8, B[8], A[8]);
  xor xor_10 (R9, B[9], A[9]);
  xor xor_11 (R10, B[10], A[10]);
  xor xor_12 (R11, B[11], A[11]);
  xor xor_13 (R12, B[12], A[12]);
  xor xor_14 (R13, B[13], A[13]);
  xor xor_15 (R14, B[14], A[14]);
  xor xor_16 (R15, B[15], A[15]);
  and and_1 (and_1_out, not_4_out, brnotEXEC);
  and and_2 (and_2_out, ADDRBUS[0], brimmed);
  and and_3 (and_3_out, ADDRBUS[2], brregdir);
  and and_4 (and_4_out, not_5_out, brnotbrorjmp);
  and and_5 (and_5_out, not_6_out, brnotFCBUS);
  or or_2 (brcnd, and_1_out, and_2_out, and_3_out, and_4_out, and_5_out);
  xor xor_17 (xor_17_out, PSW[2], PSW[3]);
  or or_3 (or_3_out, INSTRUCBUS[10], INSTRUCBUS[8]);
  and and_6 (RA0, B[0], A[0]);
  and and_7 (RA1, B[1], A[1]);
  and and_8 (RA2, B[2], A[2]);
  and and_9 (RA3, B[3], A[3]);
  and and_10 (RA4, B[4], A[4]);
  and and_11 (RA5, B[5], A[5]);
  and and_12 (RA6, B[6], A[6]);
  and and_13 (RA7, B[7], A[7]);
  or or_4 (or_4_out, xor_17_out, PSW[1]);
  and and_14 (and_14_out, INSTRUCBUS[9], PSW[4]);
  and and_15 (and_15_out, or_4_out, or_3_out);
  and and_16 (and_16_out, INSTRUCBUS[6], PSW[3]);
  Comparator comparator_1 (.a(in_11), .b(A[7:0]), .eq(equal));  // open: gt, lt
  and and_17 (RA8, B[8], A[8]);
  and and_18 (RA9, B[9], A[9]);
  and and_19 (RA10, B[10], A[10]);
  and and_20 (RA11, B[11], A[11]);
  and and_21 (RA12, B[12], A[12]);
  and and_22 (RA13, B[13], A[13]);
  and and_23 (RA14, B[14], A[14]);
  and and_24 (RA15, B[15], A[15]);
  and and_25 (and_25_out, INSTRUCBUS[7], ~PSW[4]);  // AND_Gate
  or or_5 (brorjmp, and_25_out, and_14_out, and_15_out, and_16_out);
  assign CMEMBUS[1] = incMAR ? 1'b1 : 1'bz;  // Controlled_Buffer controlled_buffer_1
  assign CREGBUS[4] = wrGPR ? 1'b1 : 1'bz;  // Controlled_Buffer controlled_buffer_2
  assign CREGBUS[9] = ldDWL ? 1'b1 : 1'bz;  // Controlled_Buffer controlled_buffer_3
  assign CREGBUS[10] = ldDWH ? 1'b1 : 1'bz;  // Controlled_Buffer controlled_buffer_4
  assign CPSW[0] = clPSWSTART ? 1'b1 : 1'bz;  // Controlled_Buffer controlled_buffer_5
  assign CPSW[1] = ldI ? 1'b1 : 1'bz;  // Controlled_Buffer controlled_buffer_6
  assign CPSW[2] = ldV ? 1'b1 : 1'bz;  // Controlled_Buffer controlled_buffer_7
  assign CPSW[3] = ldN ? 1'b1 : 1'bz;  // Controlled_Buffer controlled_buffer_8
  assign CPSW[4] = ldZ ? 1'b1 : 1'bz;  // Controlled_Buffer controlled_buffer_9
  assign CPSW[5] = ldSTART ? 1'b1 : 1'bz;  // Controlled_Buffer controlled_buffer_10
  assign CPSW[6] = ldC ? 1'b1 : 1'bz;  // Controlled_Buffer controlled_buffer_11
  assign CMEMBUS[0] = ldMAR ? 1'b1 : 1'bz;  // Controlled_Buffer controlled_buffer_12
  assign CMEMBUS[2] = ldMDR ? 1'b1 : 1'bz;  // Controlled_Buffer controlled_buffer_13
  assign CMEMBUS[3] = ldPC ? 1'b1 : 1'bz;  // Controlled_Buffer controlled_buffer_14
  assign CMEMBUS[5] = mxMAR0 ? 1'b1 : 1'bz;  // Controlled_Buffer controlled_buffer_15
  assign CMEMBUS[6] = mxMAR1 ? 1'b1 : 1'bz;  // Controlled_Buffer controlled_buffer_16
  assign CMEMBUS[7] = mxMDR0 ? 1'b1 : 1'bz;  // Controlled_Buffer controlled_buffer_17
  assign CMEMBUS[8] = mxMDR1 ? 1'b1 : 1'bz;  // Controlled_Buffer controlled_buffer_18
  assign CMEMBUS[10] = incSP ? 1'b1 : 1'bz;  // Controlled_Buffer controlled_buffer_19
  assign CMEMBUS[11] = decSP ? 1'b1 : 1'bz;  // Controlled_Buffer controlled_buffer_20
  assign CMEMBUS[12] = mxPC1 ? 1'b1 : 1'bz;  // Controlled_Buffer controlled_buffer_21
  assign CMEMBUS[13] = mxPC0 ? 1'b1 : 1'bz;  // Controlled_Buffer controlled_buffer_22
  assign CFFBUS[5] = clEXEC ? 1'b1 : 1'bz;  // Controlled_Buffer controlled_buffer_23
  assign CFFBUS[6] = stINTR ? 1'b1 : 1'bz;  // Controlled_Buffer controlled_buffer_24
  assign CMEMBUS[9] = mxMDR2 ? 1'b1 : 1'bz;  // Controlled_Buffer controlled_buffer_25
  assign CMEMBUS[14] = mxMAR2 ? 1'b1 : 1'bz;  // Controlled_Buffer controlled_buffer_26
  assign rdMEM = rdMEM_t ? 1'b1 : 1'bz;  // Controlled_Buffer controlled_buffer_27
  assign wrMEM = wrMEM_t ? 1'b1 : 1'bz;  // Controlled_Buffer controlled_buffer_28

  // Other names for the same wires on the sheet: A15__0[15:0] = A; A15__1[14:0] = A[15:1]; immed = ADDRBUS[0];
  //   regdir = ADDRBUS[2]; B15__0[15:0] = B; CLK = in_4; FCBUS = in_5; HALT = INSTRUCBUS[0]; RTS = INSTRUCBUS[1];
  //   RTI = INSTRUCBUS[2]; ROR = INSTRUCBUS[3]; PUSH = INSTRUCBUS[4]; POP = INSTRUCBUS[5]; BOVF = INSTRUCBUS[6];
  //   BNCR = INSTRUCBUS[7]; BLEQ = INSTRUCBUS[8]; BLSSU = INSTRUCBUS[9]; JLEQ = INSTRUCBUS[10]; JMP = INSTRUCBUS[11];
  //   JSR = INSTRUCBUS[12]; LD = INSTRUCBUS[13]; ST = INSTRUCBUS[14]; DEC = INSTRUCBUS[15]; SUB = INSTRUCBUS[16];
  //   XOR = INSTRUCBUS[17]; AND = INSTRUCBUS[18]; STRFIND = INSTRUCBUS[19]; MDR7__0[7:0] = in_11;
  //   EXEC = PHASEFFBUS[2]; PSWZ = PSW[1]; PSWN = PSW[2]; PSWV = PSW[3]; PSWC = PSW[4];
  //   R15__0[15:0] = {R15, R14, R13, R12, R11, R10, R9, R8, R7, R6, R5, R4, R3, R2, R1, R0};
  //   RA15__0[15:0] = {RA15, RA14, RA13, RA12, RA11, RA10, RA9, RA8, RA7, RA6, RA5, RA4, RA3, RA2, RA1, RA0};
  //   rst = in_3

  // Notes on the sheet:
  //   Upravljacka jedinica
  //   Operaciona jedinica
  //   Akumulator
  //   Uslov za skok
endmodule

module INTR (
  input  in_1,
  input  in_2,
  input  in_3,
  input  [3:0] PHASEFFBUS,
  input  [20:0] INSTRUCBUS,
  input  [15:0] PSW,
  input  [7:0] intr,
  output [15:0] ADDIVTP,
  output [2:0] UEXT2__0,
  output inta,
  output [14:0] CMEMBUS,
  output [7:0] CFFBUS,
  output [11:0] CREGBUS,
  output rdMEM,
  output wrMEM
);

  wire and_2_out, and_3_out, and_4_out, brcnd, brnotFCBUS, brnotINTR, brnotprekid, bruncnd, clINTR, incMAR,
       incSP, ldDWH, ldDWL, ldMAR, ldMDR, ldPC, mxMAR0, mxMAR1, mxMAR2, mxMDR0, mxMDR1, mxMDR2, mxPC1,
       not_1_out, not_2_out, not_3_out, not_5_out, not_6_out, not_7_out, prekid, prper, rdMEM_t,
       reg5_cl_inc_ld_1_p5, reg5_cl_inc_ld_1_p6, stFETCH, wrMEM_t;
  wire [2:0] dc3_8_1_p1;
  wire [3:1] IVTDSP15__0;
  wire [4:0] reg5_cl_inc_ld_1_p3, reg5_cl_inc_ld_1_p4;
  wire [15:0] IVTP15__0;
  wire [30:27] rom_intr_1_dout30__0;

  and and_1 (prekid, prper, PSW[15], not_2_out);
  not not_1 (not_1_out, in_1);
  // REG5_CL_INC_LD reg5_cl_inc_ld_1: pin names not known; wires that end beside it: in_2, not_1_out, reg5_cl_inc_ld_1_p3, reg5_cl_inc_ld_1_p4, reg5_cl_inc_ld_1_p5, reg5_cl_inc_ld_1_p6
  // DC3_8 dc3_8_1: pin names not known; wires that end beside it: dc3_8_1_p1, 1'b1, bruncnd, brnotINTR, brnotprekid, brnotFCBUS
  not not_2 (not_2_out, INSTRUCBUS[0]);
  not not_3 (not_3_out, in_1);
  // REG16_LD reg16_ld_1: pin names not known; wires that end beside it: in_2, not_3_out, IVTP15__0
  not not_4 (reg5_cl_inc_ld_1_p6, reg5_cl_inc_ld_1_p5);
  or or_1 (prper, intr[7], intr[6], intr[5], intr[4], intr[3], intr[2], intr[1], intr[0]);
  or or_2 (reg5_cl_inc_ld_1_p5, bruncnd, brcnd);
  ROM_INTR rom_intr_1 (
    .A5__0({1'b0, reg5_cl_inc_ld_1_p4}), .CS(1'b1),
    .DOUT30__0({rom_intr_1_dout30__0, reg5_cl_inc_ld_1_p3, dc3_8_1_p1, mxMAR2, clINTR, stFETCH, mxPC1, ldPC, ldDWH, ldDWL, incMAR, rdMEM_t, inta, mxMDR2, mxMDR0, wrMEM_t, ldMDR, mxMDR1, incSP, ldMAR, mxMAR1, mxMAR0}));  // open: DOUT36__31
  // CD8 cd8_1: pin names not known; wires that end beside it: intr[7], intr[6], intr[5], intr[4], intr[3], intr[2], intr[1], intr[0], 1'b1, UEXT2__0[2], UEXT2__0[1], UEXT2__0[0]
  // REG3_LD reg3_ld_1: pin names not known; wires that end beside it: in_2, UEXT2__0, IVTDSP15__0, IVTDSP15__0[1], inta
  // ADD16 add16_1: pin names not known; wires that end beside it: IVTP15__0, ADDIVTP, {{12{1'b0}}, IVTDSP15__0, 1'b0}, 1'b0
  not not_5 (not_5_out, PHASEFFBUS[3]);
  not not_6 (not_6_out, prekid);
  not not_7 (not_7_out, in_3);
  and and_2 (and_2_out, not_5_out, brnotINTR);
  and and_3 (and_3_out, not_6_out, brnotprekid);
  and and_4 (and_4_out, not_7_out, brnotFCBUS);
  or or_3 (brcnd, and_2_out, and_3_out, and_4_out);
  assign CMEMBUS[0] = ldMAR ? 1'b1 : 1'bz;  // Controlled_Buffer controlled_buffer_1
  assign CMEMBUS[1] = incMAR ? 1'b1 : 1'bz;  // Controlled_Buffer controlled_buffer_2
  assign CMEMBUS[2] = ldMDR ? 1'b1 : 1'bz;  // Controlled_Buffer controlled_buffer_3
  assign CMEMBUS[3] = ldPC ? 1'b1 : 1'bz;  // Controlled_Buffer controlled_buffer_4
  assign CMEMBUS[5] = mxMAR0 ? 1'b1 : 1'bz;  // Controlled_Buffer controlled_buffer_5
  assign CMEMBUS[6] = mxMAR1 ? 1'b1 : 1'bz;  // Controlled_Buffer controlled_buffer_6
  assign CMEMBUS[7] = mxMDR0 ? 1'b1 : 1'bz;  // Controlled_Buffer controlled_buffer_7
  assign CMEMBUS[8] = mxMDR1 ? 1'b1 : 1'bz;  // Controlled_Buffer controlled_buffer_8
  assign CMEMBUS[9] = mxMDR2 ? 1'b1 : 1'bz;  // Controlled_Buffer controlled_buffer_9
  assign CMEMBUS[10] = incSP ? 1'b1 : 1'bz;  // Controlled_Buffer controlled_buffer_10
  assign CMEMBUS[12] = mxPC1 ? 1'b1 : 1'bz;  // Controlled_Buffer controlled_buffer_11
  assign CMEMBUS[14] = mxMAR2 ? 1'b1 : 1'bz;  // Controlled_Buffer controlled_buffer_12
  assign CFFBUS[0] = stFETCH ? 1'b1 : 1'bz;  // Controlled_Buffer controlled_buffer_13
  assign CFFBUS[7] = clINTR ? 1'b1 : 1'bz;  // Controlled_Buffer controlled_buffer_14
  assign CREGBUS[1] = inta ? 1'b1 : 1'bz;  // Controlled_Buffer controlled_buffer_15
  assign CREGBUS[9] = ldDWL ? 1'b1 : 1'bz;  // Controlled_Buffer controlled_buffer_16
  assign CREGBUS[10] = ldDWH ? 1'b1 : 1'bz;  // Controlled_Buffer controlled_buffer_17
  assign rdMEM = rdMEM_t ? 1'b1 : 1'bz;  // Controlled_Buffer controlled_buffer_18
  assign wrMEM = wrMEM_t ? 1'b1 : 1'bz;  // Controlled_Buffer controlled_buffer_19

  // Other names for the same wires on the sheet: ldBR = inta; ADDIVTP15__0[15:0] = ADDIVTP; CLK = in_2; FCBUS = in_3;
  //   HALT = INSTRUCBUS[0]; intr7__0[7:0] = intr; INTR_t = PHASEFFBUS[3]; PSWI = PSW[15]; rst = in_1

  // Notes on the sheet:
  //   Operaciona jedinica
  //   Upravljacka jedinica
endmodule

module RAM (
  input  [15:0] in_1,
  input  in_2,
  input  [7:0] in_3,
  input  in_4,
  input  in_5,
  input  in_6,
  output [7:0] out_7,
  output out_8
);

  wire and_1_out, and_2_out, CNT0, LDCNT, not_1_out, notCNT0, or_1_out, reg4_ld_sl_sr_1_p6, rsff_2_p4,
       rsff_2_p5, rsff_3_p4, sl;
  wire [3:0] CNT, LFSR;

  // RSFF rsff_1: pin names not known; wires that end beside it: 1'b0, in_2, in_6, sl
  or or_1 (or_1_out, in_4, in_5);
  // REG4_LD_SL_SR reg4_ld_sl_sr_1: pin names not known; wires that end beside it: 1'b0, 1'b0, in_2, 4'b1111, LFSR, reg4_ld_sl_sr_1_p6, sl, in_6
  // RisingEdge risingedge_1: pin names not known; wires that end beside it: or_1_out, in_2, LDCNT
  // MEM64Kx8 mem64kx8_1: pin names not known; wires that end beside it: in_1, 1'b1, in_2, in_3, out_7, in_4
  xor xor_1 (reg4_ld_sl_sr_1_p6, LFSR[2], LFSR[3]);
  and and_1 (and_1_out, CNT0, not_1_out);
  not not_1 (not_1_out, LDCNT);
  // RSFF rsff_2: pin names not known; wires that end beside it: and_1_out, in_2, LDCNT, rsff_2_p4, rsff_2_p5
  not not_2 (rsff_2_p4, in_6);
  and and_2 (and_2_out, rsff_2_p5, CNT0);
  // REG4m_DEC_LD reg4m_dec_ld_1: pin names not known; wires that end beside it: in_2, LFSR, CNT, LDCNT, notCNT0, notCNT0
  or or_2 (notCNT0, CNT[0], CNT[1], CNT[2], CNT[3]);
  // RSFF rsff_3: pin names not known; wires that end beside it: out_8, in_2, and_2_out, rsff_3_p4, out_8
  not not_3 (rsff_3_p4, in_6);
  not not_4 (CNT0, notCNT0);

  // Other names for the same wires on the sheet: ADR[15:0] = in_1; CLK = in_2; DIN[7:0] = in_3; DOUT[7:0] = out_7;
  //   fc = out_8; RDMEM = in_5; rst = in_6; WRMEM = in_4

  // Notes on the sheet:
  //   Random broj predstavlja vreme pristupa memoriji
  //   Brojac za generisanje random broja 
  //   Jedinica za generisanje function complete (fc) signala
  //   Brojac za dekrementiranje random broja
endmodule
